# Fritzing sketch BluePrint (saved by Fritzing 0.9.3b)

parts:
  GY-NEO6MV2 = SUP500F [package=sup500f]
  Raspberry_Pi_Zero1 = Raspberry Pi Zero
  GSM_SIM_GPSR_SMS_SIM900_SIM1 = SIM800L [package=THT]

nets:
  GND: GY-NEO6MV2.RX-I, Raspberry_Pi_Zero1.GND, GSM_SIM_GPSR_SMS_SIM900_SIM1.GND
  N1: GY-NEO6MV2.TX-O, Raspberry_Pi_Zero1.3v3
  N2: GY-NEO6MV2.GND, Raspberry_Pi_Zero1.GIPO14
  N3: GY-NEO6MV2.VCC, Raspberry_Pi_Zero1.GIPO15
  5V: Raspberry_Pi_Zero1.5V, GSM_SIM_GPSR_SMS_SIM900_SIM1.5V

notes:
  GND: Black
  VCC: Red
  RX: Yellow
  TX: Green
  SIM900l
